// Logisim project SET,RESET.circ as structural Verilog: 1 circuit, main circuit main
module main (
  output OUTPUT,
  output INVERT
);

  wire RESET_out, SET_out;

  Button RESET (.out(RESET_out));
  Button SET (.out(SET_out));
  nor nor_1 (OUTPUT, RESET_out, INVERT);
  nor nor_2 (INVERT, SET_out, OUTPUT);
endmodule
